# Fritzing sketch wiring_tagtune (saved by Fritzing 0.9.6b)
perfboards: 1

parts:
  A1 = Waveshare rp2040-zero tht [package=THT]
  M1 = PAM8403 Stereo Amplifier [part_number=HW-104]
  U1 = RFID RC522 SIP - 8 pins [chip_label="RFID RC522" package="SIP (Single Inline) [THT]"]  # not connected
  DFPlayer_Mini1 = DFPlayer MINI [package="DIP (Dual Inline) [THT]"]
  J1 = JST XH_2.54mm Horizontal SMD_Connector 2pin [package=SMD]
  J3 = JST XH_2.54mm Horizontal SMD_Connector 2pin [package=SMD]  # not connected
  J4 = JST XH_2.54mm Horizontal SMD_Connector 2pin [package=SMD]  # not connected
  SP1 = SPEAKER [package=pcb_mount_speaker]  # not connected
  J5 = JST XH_2.54mm Horizontal SMD Connector 3pin [package=SMD]  # not connected
  J6 = JST XH_2.54mm Horizontal SMD_Connector 2pin [package=SMD]  # not connected
  J7 = JST XH_2.54mm Horizontal SMD Connector 3pin [package=SMD]
  J8 = JST XH_2.54mm Horizontal SMD_Connector 2pin [package=SMD]
  DFPlayer_Mini2 = DFPlayer MINI [package="DIP (Dual Inline) [THT]"]  # not connected

nets:
  N1: A1.Pin_1, M1.POWER+, J7.pin1
  N2: A1.Pin_2, DFPlayer_Mini1.GND#6
  N3: A1.Pin_3, DFPlayer_Mini1.VCC
  N4: A1.Pin_6, J7.pin3
  N5: A1.Pin_16, J1.pin1
  N6: A1.Pin_17, J8.pin1
  N7: A1.Pin_18, DFPlayer_Mini1.TX
  N8: A1.Pin_19, DFPlayer_Mini1.RX
  N9: A1.Pin_20, DFPlayer_Mini1.BUSY
  N10: M1.POWER-, DFPlayer_Mini1.GND#9
  N11: M1.INPUTL, DFPlayer_Mini1.SPK2
  N12: M1.INPUTR, DFPlayer_Mini1.SPK1

custom parts:
  Waveshare rp2040-zero tht: .RP2040-Zero, A Low-Cost, High-Performance Pico-Like MCU Board Based On Raspberry Pi Microcontroller RP2040. This varant is THT without the extra connections.
  PAM8403 Stereo Amplifier: PAM8403 stereo amplifier module Descriptive words Links: PAM8403 product datasheet
  RFID RC522 SIP - 8 pins: A SIP stand-in part for RFID RC522 . With 8 pins on a 300 mil single inline package (SIP) footprint.
  DFPlayer MINI: MP3 module by DFRobot.com for playing Music from an SD-Card. Supports WAV and MP3 files.
  JST XH_2.54mm Horizontal SMD_Connector 2pin: JST XH_2.54mm Horizontal SMD_Connector 2pin.
  JST XH_2.54mm Horizontal SMD Connector 3pin: JST XH_2.54mm Horizontal SMD Connector 3pin.
